# Fritzing sketch FinalProject (saved by Fritzing 0.9.6b)
breadboards: 1

parts:
  Q1 = Basic FET P-Channel [package="TO220 [THT]"]
  Q2 = Basic FET P-Channel [package="TO220 [THT]"]
  Q3 = Basic FET N-Channel [package="TO220 [THT]"]
  Q4 = Basic FET N-Channel [package="TO220 [THT]"]
  DC_Mot_Enc1 = DC Motor with two-phase hall-encoder [part_number=VT-E-G25A-06-177E]
  RE1 = Rotary Encoder [package=THT]
  R1 = Resistor [tolerance=±5% power=0.25 resistance=220 package=THT]
  R2 = Resistor [tolerance=±5% power=0.25 resistance=220 package=THT]
  IR1 = TSOP382, TSOP384 [package=THT]
  LED1 = 2-digit 7-segment (D2601) [package=THT-longpads]
  R10 = Resistor [tolerance=±5% power=0.25 resistance=330 package=THT]
  R11 = Resistor [tolerance=±5% power=0.25 resistance=330 package=THT]
  R12 = Resistor [tolerance=±5% power=0.25 resistance=330 package=THT]
  R13 = Resistor [tolerance=±5% power=0.25 resistance=330 package=THT]
  R14 = Resistor [tolerance=±5% power=0.25 resistance=330 package=THT]
  R15 = Resistor [tolerance=±5% power=0.25 resistance=330 package=THT]
  R16 = Resistor [tolerance=±5% power=0.25 resistance=330 package=THT]
  R17 = Resistor [tolerance=±5% power=0.25 resistance=330 package=THT]

nets:
  N1: Q1.gate, Q3.gate
  N2: Q1.drain, Q3.drain, DC_Mot_Enc1.pin6
  N3: Q1.source, Q2.source, DC_Mot_Enc1.pin2, R1.Pin_1, R2.Pin_1, IR1.VCC
  N4: Q2.gate, Q4.gate
  N5: Q2.drain, Q4.drain, DC_Mot_Enc1.pin1
  N6: Q3.source, Q4.source
  N7: DC_Mot_Enc1.pin5, RE1.EncoderPinC, IR1.GND
  N8: RE1.EncoderPinA, R2.Pin_0
  N9: RE1.EncoderPinB, R1.Pin_0
  N10: LED1.A, R12.Pin_1
  N11: LED1.C, R15.Pin_1
  N12: LED1.DP, R13.Pin_1
  N13: LED1.E, R17.Pin_1
  N14: LED1.D, R16.Pin_1
  N15: LED1.G, R14.Pin_1
  N16: LED1.F, R10.Pin_1
  N17: LED1.B, R11.Pin_1

custom parts:
  TSOP382, TSOP384: TSOP38x These products are miniaturized IR receiver modules for infrared remote control systems. A PIN diode and a preamplifier are assembled on a leadframe, the epoxy package contains an IR filter.
  2-digit 7-segment (D2601): Most common two-digit seven-segment led indicator you can find on the internet. 10 legs: 2 common electrodes (one per each digit), 8 electrodes of each segment. This variant has been modified by Zuofu Cheng to reflect the D2601 pinout.
