# Fritzing sketch ScheNBB (saved by Fritzing 0.9.4)
breadboards: 1

parts:
  R1 = Resistor [tolerance=±5% resistance=1k package=THT]
  R2 = Resistor [tolerance=±5% resistance=1k package=THT]
  IC1 = General purpose bipolar Timer [package=dil-08]
  C1 = Electrolytic Capacitor [capacitance=10µF package="100 mil [THT, electrolytic]"]
  C2 = Ceramic Capacitor [capacitance="100 nF" package="1206 [SMD, multilayer]"]

nets:
  N1: R1.Pin_0, IC1._RES, IC1.VCC+
  N2: R1.Pin_1, R2.Pin_1, IC1.DIS
  N3: R2.Pin_0, IC1.TRI, IC1.TRE, C1.+
  N4: IC1.GND, C1.-, C2.0
  N5: IC1.CON, C2.1
