# Fritzing sketch lab2Logic (saved by Fritzing 0.9.6b)
breadboards: 1

parts:
  R1 = Resistor [tolerance=±5% power=0.25 resistance=2k package=THT]
  R2 = Resistor [tolerance=±5% power=0.25 resistance=2k package=THT]
  RE1 = Rotary Encoder [package=THT]

nets:
  N1: R1.Pin_0, RE1.EncoderPinB
  N2: R1.Pin_1, R2.Pin_1
  N3: R2.Pin_0, RE1.EncoderPinA
