# Fritzing sketch lab2Potentiometer (saved by Fritzing 0.9.4)
breadboards: 1

parts:
  LED1 = 2-digit 7-segment (D2601) [package=THT-longpads]
  R1 = Resistor [tolerance=±5% power=0.25 resistance=330 package=THT]
  R3 = Resistor [tolerance=±5% power=0.25 resistance=330 package=THT]
  R4 = Resistor [tolerance=±5% power=0.25 resistance=330 package=THT]
  R5 = Resistor [tolerance=±5% power=0.25 resistance=330 package=THT]
  R6 = Resistor [tolerance=±5% power=0.25 resistance=330 package=THT]
  R7 = Resistor [tolerance=±5% power=0.25 resistance=330 package=THT]
  R8 = Resistor [tolerance=±5% power=0.25 resistance=330 package=THT]
  R9 = Resistor [tolerance=±5% power=0.25 resistance=330 package=THT]
  R10 = TRIMPOT [package=3362u-2]  # not connected

nets:
  N1: LED1.A, R7.Pin_1
  N2: LED1.C, R4.Pin_1
  N3: LED1.DP, R6.Pin_1
  N4: LED1.E, R1.Pin_1
  N5: LED1.D, R3.Pin_1
  N6: LED1.G, R5.Pin_1
  N7: LED1.F, R9.Pin_1
  N8: LED1.B, R8.Pin_1

custom parts:
  2-digit 7-segment (D2601): Most common two-digit seven-segment led indicator you can find on the internet. 10 legs: 2 common electrodes (one per each digit), 8 electrodes of each segment. This variant has been modified by Zuofu Cheng to reflect the D2601 pinout.
