# Fritzing sketch Lab4BJT (saved by Fritzing 0.9.6b)
breadboards: 1

parts:
  M1 = gear-motor
  Q1 = TRANSISTOR_NPN [package=to-92-ammo]
  R1 = Resistor [tolerance=±5% power=0.25 resistance=100 package=THT]

nets:
  N1: M1.pin_2, Q1.C
  N2: Q1.B, R1.Pin_1
