# Fritzing sketch Lab5 2 (saved by Fritzing 0.9.6b)
breadboards: 1

parts:
  R1 = Resistor [tolerance=±5% power=0.25 resistance=220 package=THT]
  C1 = Ceramic Capacitor [capacitance=10µF voltage=35V package="200 mil [THT, multilayer]"]
  DC_Mot_Enc1 = DC Motor with two-phase hall-encoder [part_number=VT-E-G25A-06-177E]
  Q1 = Basic FET N-Channel [package="TO220 [THT]"]
  RE1 = Rotary Encoder [package=THT]
  R2 = Resistor [tolerance=±5% power=0.25 resistance=220 package=THT]
  R4 = Resistor [tolerance=±5% power=0.25 resistance=220 package=THT]

nets:
  N1: R1.Pin_1, C1.1, Q1.gate
  N2: C1.0, DC_Mot_Enc1.pin5, Q1.source, RE1.EncoderPinC
  N3: DC_Mot_Enc1.pin1, DC_Mot_Enc1.pin2, R2.Pin_1, R4.Pin_1
  N4: DC_Mot_Enc1.pin6, Q1.drain
  N5: RE1.EncoderPinA, R2.Pin_0
  N6: RE1.EncoderPinB, R4.Pin_0
