# Fritzing sketch Circuit 2 (saved by Fritzing 0.9.6b)
breadboards: 1

parts:
  Q1 = Basic FET P-Channel [package="TO220 [THT]"]
  Q2 = Basic FET P-Channel [package="TO220 [THT]"]
  Q3 = Basic FET N-Channel [package="TO220 [THT]"]
  Q4 = Basic FET N-Channel [package="TO220 [THT]"]

nets:
  N1: Q1.gate, Q3.gate
  N2: Q1.drain, Q3.drain
  N3: Q1.source, Q2.source
  N4: Q2.gate, Q4.gate
  N5: Q2.drain, Q4.drain
  N6: Q3.source, Q4.source
