# Fritzing sketch Circuit 4 (saved by Fritzing 0.9.6b)
breadboards: 1

parts:
  Q1 = Basic FET P-Channel [package="TO220 [THT]"]
  Q2 = Basic FET P-Channel [package="TO220 [THT]"]
  Q3 = Basic FET N-Channel [package="TO220 [THT]"]
  Q4 = Basic FET N-Channel [package="TO220 [THT]"]
  DC_Mot_Enc1 = DC Motor with two-phase hall-encoder [part_number=VT-E-G25A-06-177E]
  RE1 = Rotary Encoder [package=THT]
  R1 = Resistor [tolerance=±5% power=0.25 resistance=220 package=THT]
  R2 = Resistor [tolerance=±5% power=0.25 resistance=220 package=THT]

nets:
  N1: Q1.gate, Q3.gate
  N2: Q1.drain, Q3.drain, DC_Mot_Enc1.pin6
  N3: Q1.source, Q2.source, DC_Mot_Enc1.pin2, R1.Pin_1, R2.Pin_1
  N4: Q2.gate, Q4.gate
  N5: Q2.drain, Q4.drain, DC_Mot_Enc1.pin1
  N6: Q3.source, Q4.source
  N7: DC_Mot_Enc1.pin5, RE1.EncoderPinC
  N8: RE1.EncoderPinA, R2.Pin_0
  N9: RE1.EncoderPinB, R1.Pin_0
